# Fritzing sketch Untitled Sketch (saved by Fritzing 0.8.7b)
breadboards: 1

parts:
  OLED1 = OLED 128x64 I2C Monochrome Display
  Teensy_3_1 = Teensy 3.1  # not connected
  S1 = Pushbutton [package="[THT]"]

nets:
  N1: OLED1.VDD, S1.Pin_3, S1.Pin_4
  N2: S1.Pin_1, S1.Pin_2
