# Fritzing sketch schematic fritz EMBEDDED (saved by Fritzing 0.8.7b)
breadboards: 1

parts:
  OLED1 = OLED 128x64 I2C Monochrome Display
  Teensy_3_1 = Teensy 3.1
  U1 = POT [package=pot_alpha_rv16af-20]
  S1 = Pushbutton [package="[THT]"]

nets:
  GND: OLED1.GND, Teensy_3_1.GND, U1.A
  VDD: OLED1.VDD, Teensy_3_1.Vin, U1.E
  N1: OLED1.SCK, Teensy_3_1.A14/DAC
  N2: OLED1.SDA, Teensy_3_1.Program
  N3: Teensy_3_1.D10, S1.Pin_3, S1.Pin_4
  N4: Teensy_3_1.D12, U1.S
